// Logisim project relogio.circ as structural Verilog: 5 circuits, main circuit contador4bits
module main (
  input  in_1
);

  wire clock_1_out, decodificador4bin_0_9dec_1_a, decodificador4bin_0_9dec_1_b, decodificador4bin_0_9dec_1_c,
       decodificador4bin_0_9dec_1_d, decodificador4bin_0_9dec_1_e, decodificador4bin_0_9dec_1_f,
       decodificador4bin_0_9dec_1_out_11, undriven, undriven_2, undriven_3, undriven_4, undriven_5,
       undriven_6, undriven_7, undriven_8, undriven_9, undriven_10, undriven_11, undriven_12, undriven_13,
       undriven_14, undriven_15, undriven_16, undriven_17, undriven_18, undriven_19, undriven_20,
       undriven_21, undriven_22, undriven_23, undriven_24;

  decodificador4bin_0_9dec decodificador4bin_0_9dec_1 (
    .in_1(undriven), .in_2(undriven_2), .in_3(undriven_3), .in_4(undriven_4),
    .a(decodificador4bin_0_9dec_1_a), .b(decodificador4bin_0_9dec_1_b), .c(decodificador4bin_0_9dec_1_c),
    .d(decodificador4bin_0_9dec_1_d), .e(decodificador4bin_0_9dec_1_e), .f(decodificador4bin_0_9dec_1_f),
    .out_11(decodificador4bin_0_9dec_1_out_11));
  _7_Segment_Display u_7_segment_display_1 (
    .g(decodificador4bin_0_9dec_1_out_11), .f(decodificador4bin_0_9dec_1_f),
    .a(decodificador4bin_0_9dec_1_a), .b(decodificador4bin_0_9dec_1_b), .e(decodificador4bin_0_9dec_1_e),
    .d(decodificador4bin_0_9dec_1_d), .c(decodificador4bin_0_9dec_1_c));  // open: dp
  Clock clock_1 (.out(clock_1_out));
  decodificador4bin_0_9dec decodificador4bin_0_9dec_2 (
    .in_1(undriven_5), .in_2(undriven_6), .in_3(undriven_7), .in_4(undriven_8));  // open: a, b, c, d, e, f, out_11
  contador_completo contador_completo_1 (
    .PRESET(in_1), .CLK(clock_1_out), .VCC(1'b1), .in_1(undriven), .in_2(undriven_2), .in_3(undriven_3),
    .in_4(undriven_4), .in_5(undriven_5), .in_6(undriven_6), .in_7(undriven_7), .in_8(undriven_8),
    .in_9(undriven_9), .in_10(undriven_10), .in_11(undriven_11), .in_12(undriven_12), .in_13(undriven_18),
    .in_14(undriven_19), .in_15(undriven_20), .in_16(undriven_21), .in_17(undriven_13), .in_18(undriven_14),
    .in_19(undriven_15), .in_20(undriven_22), .in_21(undriven_16), .in_22(undriven_23), .in_23(undriven_17),
    .in_24(undriven_24));
  decodificador4bin_0_9dec decodificador4bin_0_9dec_3 (
    .in_1(undriven_9), .in_2(undriven_10), .in_3(undriven_11), .in_4(undriven_12));  // open: a, b, c, d, e, f, out_11
  decodificador4bin_0_9dec decodificador4bin_0_9dec_4 (
    .in_1(undriven_18), .in_2(undriven_19), .in_3(undriven_20), .in_4(undriven_21));  // open: a, b, c, d, e, f, out_11
  decodificador4bin_0_9dec decodificador4bin_0_9dec_5 (
    .in_1(undriven_13), .in_2(undriven_14), .in_3(undriven_15), .in_4(undriven_22));  // open: a, b, c, d, e, f, out_11
  decodificador4bin_0_9dec decodificador4bin_0_9dec_6 (
    .in_1(undriven_16), .in_2(undriven_23), .in_3(undriven_17), .in_4(undriven_24));  // open: a, b, c, d, e, f, out_11
endmodule

module contador4bits (
  input  PRESET,
  input  CLK,
  input  VCC,
  output Q1,
  output Q2,
  output Q3,
  output Q4,
  output SOUT
);

  wire fliflopjk_1_out_7, fliflopjk_2_out_7, fliflopjk_3_out_7;

  and and_1 (SOUT, Q4, fliflopjk_3_out_7, Q2, fliflopjk_1_out_7);
  fliflopjk fliflopjk_1 (
    .PRESET(PRESET), .J(VCC), .CLK(CLK), .K(VCC), .CLEAR(SOUT), .out_6(Q1), .out_7(fliflopjk_1_out_7));
  fliflopjk fliflopjk_2 (
    .PRESET(PRESET), .J(VCC), .CLK(fliflopjk_1_out_7), .K(VCC), .CLEAR(SOUT), .out_6(Q2),
    .out_7(fliflopjk_2_out_7));
  fliflopjk fliflopjk_3 (
    .PRESET(PRESET), .J(VCC), .CLK(fliflopjk_2_out_7), .K(VCC), .CLEAR(SOUT), .out_6(Q3),
    .out_7(fliflopjk_3_out_7));
  fliflopjk fliflopjk_4 (
    .PRESET(PRESET), .J(VCC), .CLK(fliflopjk_3_out_7), .K(VCC), .CLEAR(SOUT), .out_6(Q4));  // open: out_7
endmodule

module fliflopjk (
  input  PRESET,
  input  J,
  input  CLK,
  input  K,
  input  CLEAR,
  output out_6,
  output out_7
);

  wire nand_1_out, nand_2_out, nand_3_out, nand_4_out, nand_5_out, nand_6_out, not_1_out, not_2_out,
       not_3_out, or_1_out;

  not not_1 (not_1_out, or_1_out);
  or or_1 (or_1_out, PRESET, CLEAR);
  not not_2 (not_2_out, CLK);
  nand nand_1 (nand_1_out, out_7, J, not_2_out);
  nand nand_2 (nand_2_out, not_2_out, K, out_6);
  nand nand_3 (nand_3_out, 1'b1, nand_1_out, nand_4_out);
  nand nand_4 (nand_4_out, nand_3_out, nand_2_out, not_1_out);
  nand nand_5 (nand_5_out, not_1_out, nand_3_out, not_3_out);
  not not_3 (not_3_out, not_2_out);
  nand nand_6 (nand_6_out, not_3_out, nand_4_out, 1'b1);
  nand nand_7 (out_6, 1'b1, nand_5_out, out_7);
  nand nand_8 (out_7, out_6, nand_6_out, not_1_out);
endmodule

module contador_completo (
  input  in_1,
  input  in_2,
  input  in_3,
  input  in_4,
  input  in_5,
  input  in_6,
  input  in_7,
  input  in_8,
  input  in_9,
  input  in_10,
  input  in_11,
  input  in_12,
  input  in_13,
  input  in_14,
  input  in_15,
  input  in_16,
  input  in_17,
  input  in_18,
  input  in_19,
  input  in_20,
  input  in_21,
  input  in_22,
  input  in_23,
  input  in_24,
  input  PRESET,
  input  CLK,
  input  VCC
);

  wire contador4bits_1_sout, contador4bits_2_sout, contador4bits_3_sout, contador4bits_4_sout,
       contador4bits_5_p8;

  contador4bits contador4bits_1 (
    .SOUT(contador4bits_1_sout), .Q1(in_1), .Q2(in_2), .Q3(in_3), .Q4(in_4), .CLK(CLK), .PRESET(PRESET),
    .VCC(VCC));
  contador4bits contador4bits_2 (
    .SOUT(contador4bits_2_sout), .Q1(in_5), .Q2(in_6), .Q3(in_7), .Q4(in_8), .CLK(contador4bits_1_sout),
    .PRESET(PRESET), .VCC(VCC));
  contador4bits contador4bits_3 (
    .SOUT(contador4bits_3_sout), .Q1(in_9), .Q2(in_10), .Q3(in_11), .Q4(in_12), .CLK(contador4bits_2_sout),
    .PRESET(PRESET), .VCC(VCC));
  contador4bits contador4bits_4 (
    .SOUT(contador4bits_4_sout), .Q1(in_13), .Q2(in_14), .Q3(in_15), .Q4(in_16), .CLK(contador4bits_3_sout),
    .PRESET(PRESET), .VCC(VCC));
  // contador4bits contador4bits_5: pin names not known; wires that end beside it: in_17, PRESET, contador4bits_4_sout, VCC, in_18, in_19, in_20, contador4bits_5_p8
  contador4bits contador4bits_6 (
    .Q1(in_21), .Q2(in_22), .Q3(in_23), .Q4(in_24), .CLK(contador4bits_5_p8), .PRESET(PRESET), .VCC(VCC));  // open: SOUT
endmodule

module decodificador4bin_0_9dec (
  input  in_1,
  input  in_2,
  input  in_3,
  input  in_4,
  output a,
  output b,
  output c,
  output d,
  output e,
  output f,
  output out_11
);

  wire and_1_out, and_2_out, and_3_out, and_4_out, and_5_out, and_6_out, not_1_out, not_2_out, not_3_out,
       not_4_out;

  not not_1 (not_1_out, in_1);
  not not_2 (not_2_out, in_2);
  not not_3 (not_3_out, in_3);
  not not_4 (not_4_out, in_4);
  and and_1 (and_1_out, not_1_out, not_2_out, not_3_out);
  and and_2 (and_2_out, not_1_out, in_2, not_4_out);
  or or_1 (a, and_1_out, and_2_out, and_3_out);
  and and_3 (and_3_out, in_1, not_3_out, not_4_out);
  and and_4 (and_4_out, in_1, not_3_out, in_4);
  and and_5 (and_5_out, not_1_out, not_2_out, not_4_out);
  or or_2 (b, and_1_out, and_5_out, and_4_out);
  or or_3 (c, and_1_out, and_5_out, and_4_out);
  or or_4 (d, and_1_out, and_5_out, and_4_out);
  or or_5 (e, and_1_out, and_5_out, and_6_out);
  and and_6 (and_6_out, in_1, not_3_out, not_4_out);
  or or_6 (f, and_1_out, and_5_out, and_4_out);
  or or_7 (out_11, and_1_out, and_6_out);
endmodule
